# Fritzing sketch Weatherbug r1.2 (saved by Fritzing 0.9.2b)
breadboards: 1

parts:
  U1 = atmega328 [part_number="Fues set to 8MHz using internal RC" package=dip]
  DHT1 = Humidity and Temperature Sensor DHT11
  R1 = Resistor [tolerance=±5% resistance=5k package=THT]
  MCP1700-1802E/TO1 = Voltage Regulator - 3.3V [package=TO-92-3]
  C1 = Ceramic Capacitor [capacitance=10µF voltage=10V package="0805 [SMD, multilayer]"]
  C2 = Ceramic Capacitor [capacitance=1µF voltage=10V package="0805 [SMD, multilayer]"]
  R2 = Resistor [tolerance=±5% resistance=10k part_number="Reset pullup" package=THT]
  R3 = Resistor [tolerance=±5% resistance=10k package=THT]
  D1 = LTE-302 [package=lte-302]
  U2 = 2.4GHz Low Power Transceiver [package=qfn20]
  S1 = SWITCH-MOMENTARY-2 [part_number="Reset switch" package=tactile_switch_tall]
  R4 = Resistor [tolerance=±5% resistance=10k part_number=Spannungsteiler2 package="2010 [SMD]"]
  R5 = Resistor [tolerance=±5% resistance=50k part_number=Spannungsteiler1 package="2010 [SMD]"]
  JP1 = Jumper [part_number="LED jumper" package=sj_2s]
  JP2 = JUMPER-3-OLD [part_number="VCC jumper" package=sj_3_paste2_3]
  J2 = Screw terminal - 2 pins [part_number="4.5-5V DC" package=THT]
  C3 = Ceramic Capacitor [capacitance="100 nF" package="1206 [SMD, multilayer]"]

nets:
  N1: U1.RESET, R2.Pin_0, S1.2
  N2: U1.VCC, JP2.2
  GND: U1.GND, DHT1.GND, MCP1700-1802E/TO1.GND, C1.0, C2.0, U2.VSS, S1.1, JP1.1, J2.pin1, C3.0
  N3: U1.D5_(PWM), DHT1.Vcc, R1.Pin_0
  N4: U1.D6_(PWM), DHT1.Data-signal, R1.Pin_1
  N5: U1.D7, R4.Pin_1
  N6: U1.D8, U2.IRQ
  N7: U1.D9_(PWM), U2.CE
  N8: U1.D10_(PWM), U2.CSN
  N9: U1.D11_(PWM), U2.MOSI
  N10: U1.D12, U2.MISO
  N11: U1.D13, R3.Pin_1, U2.SCK
  N12: U1.AVCC, MCP1700-1802E/TO1.output_voltage, C2.1, R2.Pin_1, U2.VDD, JP2.1
  N13: U1.AREF, C3.1
  N14: U1.A0, R4.Pin_0, R5.Pin_1
  N15: MCP1700-1802E/TO1.input_voltage, R5.Pin_0, JP2.3, J2.pin2
  N16: R3.Pin_0, D1.A
  N17: D1.C, JP1.2

custom parts:
  Humidity and Temperature Sensor DHT11: Digital relative humidity & temperature sensor DHT11
  Voltage Regulator - 3.3V: 3.3V DC Voltage Regulator
